# Fritzing sketch co2 (saved by Fritzing 0.9.3b)
breadboards: 2

parts:
  U3 = NodeMCU V1.0
  Onderdeel2 = OLED Monochrome 128x64 0.96 inch [part_number=326]
  TD-er1 = MH-Z19 CO2 sensor [part_number=MH-Z19]
  OLED1 = 128x64 Monochrom OLED Display with SPI Control  # not connected
  U4 = NodeMCU V1.0
  TD-er2 = MH-Z19 CO2 sensor [part_number=MH-Z19]
  OLED_I2C1 = OLED 128x64 I2C Monochrome Display

nets:
  N1: U3.D0, Onderdeel2.DC_SA0
  N2: U3.D1, Onderdeel2.CS
  N3: U3.D2, TD-er1.TX
  3V3: U3.3V3, Onderdeel2.3.3V
  GND: U3.GND, Onderdeel2.GND, TD-er1.GND
  N4: U3.D5, Onderdeel2.SCLK_SCK
  N5: U3.D7, Onderdeel2.MOSI_SDA
  N6: U3.D8, TD-er1.RX
  VIN: U3.Vin, TD-er1.Vin
  N7: U3.SD3, Onderdeel2.RESET
  N8: U4.D1, OLED_I2C1.SCK
  N9: U4.D2, TD-er2.TX
  GND_2: U4.GND, TD-er2.GND, OLED_I2C1.GND
  N10: U4.D8, TD-er2.RX
  VIN_2: U4.Vin, TD-er2.Vin
  N11: U4.SD3, OLED_I2C1.SDA

custom parts:
  NodeMCU V1.0: ESP8266 based NodeMCU
  OLED Monochrome 128x64 0.96 inch: These displays are small, only about 1" diameter, but very readable due to the high contrast of an OLED display. This display is made of 128x64 individual white OLED pixels, each one is turned on or off by the controller chip. Because the display makes its own light, no backlight is required. This reduces the power required to run the OLED and is why the display has such high contrast; we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
